# Fritzing sketch wiring-pwm (saved by Fritzing 1.0.3b)
breadboards: 1

parts:
  M1 = xy-mos d4184 [package=THT]
  Heater_(GND/PWM) = Screw terminal - 2 pins [package=THT]
  MCU1 = Raspberry Pi Zero

nets:
  N1: M1.pin1, M1.pin3, MCU1.pin_12
  GND: M1.pin2, M1.pin7, MCU1.pin_14, MCU1.pin_30, MCU1.pin_39
  12V: M1.pin8
  N2: M1.pin9, Heater_(GND/PWM).pin1
  N3: M1.pin10, Heater_(GND/PWM).pin2

custom parts:
  xy-mos d4184: xy-mos d4184 Two parallel N-Channel logic compatible MOSFETS with low Rds(on) for high current low-side switching applications.
